// Logisim project Digital Vending Machine.circ as structural Verilog: 2 circuits, main circuit Digital Vending Machine
module Digital_Vending_Machine (
);

  wire _1_out, _2_out, _5_out, _10_out, _20_out, _50_out, _100_out, Cancel_out;

  Button _1 (.out(_1_out));
  Button _2 (.out(_2_out));
  Button _5 (.out(_5_out));
  Button _10 (.out(_10_out));
  Button _20 (.out(_20_out));
  Button _50 (.out(_50_out));
  Button _100 (.out(_100_out));
  Button Cancel (.out(Cancel_out));
  Insert_Money insert_money_1 (
    ._1(_1_out), ._2(_2_out), ._5(_5_out), ._10(_10_out), ._20(_20_out), ._50(_50_out), ._100(_100_out),
    .Clear(Cancel_out));  // open: out_9, out_10, out_12, out_11, out_13, out_14, out_15, out_16
endmodule

module Insert_Money (
  input  Clear,
  input  _1,
  input  _2,
  input  _5,
  input  _10,
  input  _20,
  input  _50,
  input  _100,
  output out_9,
  output out_10,
  output out_11,
  output out_12,
  output out_13,
  output out_14,
  output out_15,
  output out_16
);

  wire adder_1_cout, adder_1_out, adder_2_cout, adder_2_out, adder_3_cout, adder_3_out, adder_4_cout,
       adder_4_out, adder_5_cout, adder_5_out, adder_6_cout, adder_6_out, adder_7_cout, adder_7_out,
       adder_8_cout, adder_8_out, LSB_out, nor_1_out, or_1_out, or_2_out, or_3_out, or_4_out;

  or or_1 (or_1_out, _100, _50);
  or or_2 (or_2_out, _50, _20);
  or or_3 (or_3_out, _100, _20, _5);
  or or_4 (or_4_out, _50, _10, _2);
  or LSB (LSB_out, _5, _1);
  nor nor_1 (nor_1_out, adder_1_cout, _100, _50, _20, _10, _5, _2, _1);
  Adder #(.width(1)) adder_1 (.a(out_9), .b(1'b0), .out(adder_1_out), .cin(adder_2_cout), .cout(adder_1_cout));
  Adder #(.width(1)) adder_2 (.a(out_10), .b(_100), .out(adder_2_out), .cin(adder_3_cout), .cout(adder_2_cout));
  Adder #(.width(1)) adder_3 (.a(out_11), .b(or_1_out), .out(adder_3_out), .cin(adder_4_cout), .cout(adder_3_cout));
  Adder #(.width(1)) adder_4 (.a(out_12), .b(or_2_out), .out(adder_4_out), .cin(adder_5_cout), .cout(adder_4_cout));
  Adder #(.width(1)) adder_5 (.a(out_13), .b(_10), .out(adder_5_out), .cin(adder_6_cout), .cout(adder_5_cout));
  Adder #(.width(1)) adder_6 (.a(out_14), .b(or_3_out), .out(adder_6_out), .cin(adder_7_cout), .cout(adder_6_cout));
  Adder #(.width(1)) adder_7 (.a(out_15), .b(or_4_out), .out(adder_7_out), .cin(adder_8_cout), .cout(adder_7_cout));
  Adder #(.width(1)) adder_8 (.a(out_16), .b(LSB_out), .out(adder_8_out), .cin(1'b0), .cout(adder_8_cout));
  D_Flip_Flop d_ff_1 (.clk(nor_1_out), .D(adder_1_out), .Q(out_9), .reset(Clear));  // open: Qn, preset, en
  D_Flip_Flop d_ff_2 (.clk(nor_1_out), .D(adder_2_out), .Q(out_10), .reset(Clear));  // open: Qn, preset, en
  D_Flip_Flop d_ff_3 (.clk(nor_1_out), .D(adder_3_out), .Q(out_11), .reset(Clear));  // open: Qn, preset, en
  D_Flip_Flop d_ff_4 (.clk(nor_1_out), .D(adder_4_out), .Q(out_12), .reset(Clear));  // open: Qn, preset, en
  D_Flip_Flop d_ff_5 (.clk(nor_1_out), .D(adder_5_out), .Q(out_13), .reset(Clear));  // open: Qn, preset, en
  D_Flip_Flop d_ff_6 (.clk(nor_1_out), .D(adder_6_out), .Q(out_14), .reset(Clear));  // open: Qn, preset, en
  D_Flip_Flop d_ff_7 (.clk(nor_1_out), .D(adder_7_out), .Q(out_15), .reset(Clear));  // open: Qn, preset, en
  D_Flip_Flop d_ff_8 (.clk(nor_1_out), .D(adder_8_out), .Q(out_16), .reset(Clear));  // open: Qn, preset, en
endmodule
